# Fritzing sketch Fan_control_using_potentiometer (saved by Fritzing 0.9.4)
breadboards: 1

parts:
  R1 = Rotary Potentiometer (Small) [maximum_resistance=100kΩ package=THT]
  DI1 = 7-Segment LED Display [package=THT]
  IC1 = L293D [package=THT]
  R2 = Resistor [tolerance=±5% resistance=220 package=THT]
  R3 = Resistor [tolerance=±5% resistance=220 package=THT]
  R4 = Resistor [tolerance=±5% resistance=220 package=THT]
  R5 = Resistor [tolerance=±5% resistance=220 package=THT]
  R6 = Resistor [tolerance=±5% resistance=220 package=THT]
  R7 = Resistor [tolerance=±5% resistance=220 package=THT]
  R8 = Resistor [tolerance=±5% resistance=220 package=THT]
  R9 = Resistor [tolerance=±5% resistance=220 package=THT]
  Part1 = Arduino Uno (Rev3)
  HC-SR04_Sensor_1 = HC-SR04 Ultrasonic Distance Sensor
  M1 = DC Motor
  VCC1 = Battery block 9V

nets:
  5V: R1.leg1, IC1.+Vmotor, Part1.5V, HC-SR04_Sensor_1.VCC
  N1: R1.wiper, Part1.A0
  GND: R1.leg2, DI1.commAnode#7, IC1.0V, Part1.GND, HC-SR04_Sensor_1.GND, VCC1.-
  N2: DI1.cathodeE, R7.Pin_1
  N3: DI1.cathodeD, R9.Pin_1
  N4: DI1.cathodeC, R8.Pin_0
  N5: DI1.cathodeDP, R6.Pin_0
  N6: DI1.cathodeB, R2.Pin_0
  N7: DI1.cathodeA, R5.Pin_0
  N8: DI1.cathodeF, R4.Pin_1
  N9: DI1.cathodeG, R3.Pin_1
  N10: IC1.Enable_2, Part1.D5_PWM
  N11: IC1.In_3, Part1.D6_PWM
  N12: IC1.Out_3_(_Controlled_by_Enable_2_), M1.pin_2
  N13: IC1.Out_4_(_Controlled_by_Enable_2_), M1.pin_1
  N14: IC1.In_4, Part1.D4
  N15: IC1.+V, VCC1.+
  N16: R2.Pin_1, Part1.D8
  N17: R3.Pin_0, Part1.D13/SCK
  N18: R4.Pin_0, Part1.D12/MISO
  N19: R5.Pin_1, Part1.D7
  N20: R6.Pin_1, Part1.D9_PWM
  N21: R7.Pin_0, Part1.D10_PWM/SS, Part1.D11_PWM/MOSI
  N22: Part1.D2, HC-SR04_Sensor_1.ECHO
  N23: Part1.D3_PWM, HC-SR04_Sensor_1.TRIG

// code stored in the sketch: Untitled2.ino
// Motor controller connections
int enA = 5;
int in1 = 6;
int in2 = 4;

//Potentiometer connections
int pot = A0; // assigns analog input A0 to variable pot
int c1 = 0;   // declares variable c1

//ultrasonic Sensor connections
#define echoPin 2 // attach pin D2 Arduino to pin Echo of HC-SR04
#define trigPin 3 //attach pin D3 Arduino to pin Trig of HC-SR04

void setup()
{
    // Set all the motor control pins to outputs
    pinMode(enA, OUTPUT);
    pinMode(in1, OUTPUT);
    pinMode(in2, OUTPUT);
    //set the potentiometer pin as input
    pinMode(pot, INPUT);
    //set Trig as output and echo as input
    pinMode(trigPin, OUTPUT);
    pinMode(echoPin, INPUT);
    // Turn off motors - Initial state
    digitalWrite(in1, LOW);
    digitalWrite(in2, LOW);
    //set all pins 7-13 as output for 7 segment display
    pinMode(7, OUTPUT);
    pinMode(8, OUTPUT);
    pinMode(9, OUTPUT);
    pinMode(10, OUTPUT);
    pinMode(11, OUTPUT);
    pinMode(12, OUTPUT);
    pinMode(13, OUTPUT);
    //set all the pins 7-13 as Low initially
    digitalWrite(7, LOW);
    digitalWrite(8, LOW);
    digitalWrite(9, LOW);
    digitalWrite(10, LOW);
    digitalWrite(11, LOW);
    digitalWrite(12, LOW);
    digitalWrite(13, LOW);
}

void loop()
{
    int duration, distance;
    // Output pulse with 1ms width on trigPin
    digitalWrite(trigPin, HIGH);
    delay(1);
    digitalWrite(trigPin, LOW);
    // Measure the pulse input in echo pin
    duration = pulseIn(echoPin, HIGH);
    // Distance is half the duration devided by 29.1 (from datasheet)
    distance = (duration / 2) / 29.1;
    // if distance less than 0.2 meter and more than 0
    if (distance <= 50 && distance >= 0)
    {
        Serial.println("Obstacle Detected!!! Remove It");
    }
    else
    {
        directionControl();
    }
}

// This function lets you control spinning direction of motor and
void directionControl()
{
    c1 = analogRead(pot);
    //display speed as per the potentiometer input
    display(c1);
    //set speed of motor as per the potentiometer input
    analogWrite(enA, c1);
    // Turn on the motor
    digitalWrite(in1, HIGH);
    digitalWrite(in2, LOW);
    delay(2000);

    // Now change motor direction
    digitalWrite(in1, LOW);
    digitalWrite(in2, HIGH);
    delay(2000);

    // Turn off the motor
    digitalWrite(in1, LOW);
    digitalWrite(in2, LOW);
}

void display(int c1)
{
    //to display 1
    if (c1 < 500)
    {
        digitalWrite(7, LOW);
        digitalWrite(8, HIGH);
        digitalWrite(9, HIGH);
        digitalWrite(10, LOW);
        digitalWrite(11, LOW);
        digitalWrite(12, LOW);
        digitalWrite(13, LOW);
    }
    //to display 2
    else if (c1 >= 500 && c1 < 1000)
    {
        digitalWrite(7, HIGH);
        digitalWrite(8, HIGH);
        digitalWrite(9, LOW);
        digitalWrite(10, HIGH);
        digitalWrite(11, HIGH);
        digitalWrite(12, LOW);
        digitalWrite(13, HIGH);
    }
    //to display 3
    else
    {
        digitalWrite(7, HIGH);
        digitalWrite(8, HIGH);
        digitalWrite(9, HIGH);
        digitalWrite(10, HIGH);
        digitalWrite(11, LOW);
        digitalWrite(12, LOW);
        digitalWrite(13, HIGH);
    }
}
