# Fritzing sketch Sonar.fzz (saved by Fritzing 0.9.4)
breadboards: 1

parts:
  Part1 = Arduino Uno (Rev3)
  R1 = Resistor [tolerance=±5% resistance=220 package=THT]
  R2 = Resistor [tolerance=±5% resistance=220 package=THT]
  R3 = Photocell (LDR) [package=THT]
  R4 = Temperature Sensor (Thermistor) [thermistor_type=NTC package=THT]
  R5 = Rotary Potentiometer (Small) [maximum_resistance=100kΩ package=THT]
  J1 = Basic Servo
  HC-SR04_Sensor_1 = HC-SR04 Ultrasonic Distance Sensor

nets:
  N1: Part1.A0, R1.Pin_0, R4.pin_1
  N2: Part1.A1, R2.Pin_0, R3.pin_1
  N3: Part1.A2, R5.wiper
  N4: Part1.D2, HC-SR04_Sensor_1.ECHO
  N5: Part1.D3_PWM, HC-SR04_Sensor_1.TRIG
  N6: Part1.D4, J1.pulse
  VCC: Part1.5V, R3.pin_0, R4.pin_0, R5.leg1, J1.vcc, HC-SR04_Sensor_1.VCC
  GND: Part1.GND, R1.Pin_1, R2.Pin_1, R5.leg2, J1.gnd, HC-SR04_Sensor_1.GND

// code stored in the sketch: Sonar.ino
#include <Servo.h>
const int trigPin = 3;
const int echoPin = 2;
long duration; // variable for the duration of sound wave travel
int distance; // variable for the distance measurement
int sensorPin = A1;
int potpin = A2;
int therm=A0;
int val;
int lightCal;

int Vo;
float R1 = 10000;
float logR2, R2, T;
float c1 = 1.009249522e-03, c2 = 2.378405444e-04, c3 = 2.019202697e-07;

Servo myServo; 
void setup() {
   Serial.begin(9600);
  myServo.attach(4);
  pinMode(trigPin, OUTPUT); // Sets the trigPin as an OUTPUT
  pinMode(echoPin, INPUT); // Sets the echoPin as an INPUT
}

void loop() {
 val = analogRead(potpin); 
 val = map(val, 0, 1023, 0, 180);// scale it for use with the servo (value between 0 and 180)  
  myServo.write(val);                  // sets the servo position according to the scaled value
  delay(15);
  
  func();
}

void func()
{
  digitalWrite(trigPin, LOW);
  delayMicroseconds(2);
  digitalWrite(trigPin, HIGH);
  delayMicroseconds(10);
  digitalWrite(trigPin, LOW);
  Vo = analogRead(therm);
  val = analogRead(potpin); 
  int temp = analogRead(therm);
  int light = analogRead(sensorPin);// reads the value of the potentiometer (value between 0 and 1023) 
  R2 = R1 * (1023.0 / (float)Vo - 1.0);
  logR2 = log(R2);
  T = (1.0 / (c1 + c2*logR2 + c3*logR2*logR2*logR2));
  T = T - 273.15;
  T = (T * 9.0)/ 5.0 + 32.0; 
  
  duration = pulseIn(echoPin, HIGH);
  lightCal = analogRead(sensorPin);
  distance = duration * 0.034 / 2;
  char pot_text[30];
  char light_text[30];
  char temp_text[30];
  char distance_text[30];

  dtostrf(val, 10, 10, pot_text);
  dtostrf(light, 10, 10, light_text);
  dtostrf(temp, 10, 10, temp_text);
  dtostrf(distance, 10, 10, distance_text);
  
  char text[125];
  snprintf(text, 125, "%s,%s,%s,%s", pot_text, light_text, temp_text, distance_text);
  Serial.println(text);
}
