# Fritzing sketch ambient_temp_control (saved by Fritzing 0.9.4)
breadboards: 1

parts:
  Part1 = Arduino Uno (Rev3)
  Part2 = Humidity Temperature Sensor SHT15  # not connected
  M1 = DC Motor
  KY-1 = Keyes Relay [package=THT]
  KY-2 = Keyes Relay [package=THT]
  VCC1 = Battery block 9V
  VCC2 = Battery block 9V
  R1 = Heating Pad

nets:
  N1: Part1.D2, KY-1.signal
  N2: Part1.D3_PWM, KY-2.signal
  N3: Part1.5V, KY-1.power, KY-2.power
  N4: Part1.GND, KY-1.ground, KY-2.ground
  N5: M1.pin_1, KY-1.C
  N6: M1.pin_2, VCC1.-
  N7: KY-1.NO, VCC1.+
  N8: KY-2.C, R1.pin_0
  N9: KY-2.NO, VCC2.+
  N10: VCC2.-, R1.pin_1

custom parts:
  Keyes Relay: The Keyes 5V relay module is suitable for SCM development, home appliance control. It uses a 5V~12V TIL control signal which can control DC / AC signal.
  Heating Pad: A thermoresistant material with an embeded conductor that dissipates electrical energy into heat.

// code stored in the sketch: ambient_temp_control.ino
const int heater = 2, fan = 3;
int Ro = 50, B =  3950, Rseries = 10;
float To = 298.15;
int optimum = 25, variation = 2;
void setup() {
  pinMode(heater, OUTPUT);
  pinMode(fan, OUTPUT);
}

void loop() {
  float Vi = analogRead(A0) * (5.0 / 1023.0);
  float R = (Vi * Rseries) / (5 - Vi);
  float T =  1 / ((1 / To) + ((log(R / Ro)) / B));
  float Tc = T - 273.15;
  //For optimum temperature 25 and variation 2.
  //Heater control
  if (Tc <= (optimum - variation)) {
    //Below or equal 23 : heater ON
    digitalWrite(heater, HIGH);
  } else if (Tc >= optimum) {
    //Above or equal to 25 : heater OFF
    digitalWrite(heater, LOW);
  }
  //Fan control
  if (Tc >= (optimum + variation)) {
    //Above or equal to 27 : fan ON
    digitalWrite(fan, HIGH);
  } else if (Tc <= optimum) {
    //Below or equal to 25 : fan OFF
    digitalWrite(fan, LOW);
  }
  delay(1000);
}
